# Fritzing sketch FINAL_03 (saved by Fritzing 0.9.3b)
breadboards: 1

parts:
  A1 = MH-FMD buzzer
  元件1 = node32s
  S1 = Pushbutton [package="[THT]"]
  S2 = Pushbutton [package="[THT]"]
  S3 = Pushbutton [package="[THT]"]
  Grove1 = Grove OLED 128x96
  U1 = WS2812 RGB LED strip
  R1 = Resistor [tolerance=±5% resistance=220 package=THT]
  R2 = Resistor [tolerance=±5% resistance=220 package=THT]
  R3 = Resistor [tolerance=±5% resistance=220 package=THT]

nets:
  5V: A1.Pin_1, 元件1.5V, U1.VCC
  N1: A1.Pin_2, 元件1.IO16
  N2: A1.Pin_3, 元件1.V_BATT, U1.GND
  3.3V: 元件1.3.3V, Grove1.VCC
  N3: 元件1.IO32, S1.Pin_1, S1.Pin_2
  N4: 元件1.IO33, S2.Pin_1, S2.Pin_2
  N5: 元件1.IO26, U1.DIN
  N6: 元件1.IO27, S3.Pin_1, S3.Pin_2
  GND: 元件1.GND, Grove1.GND, R1.Pin_1, R2.Pin_1, R3.Pin_1
  N7: 元件1.IO22, Grove1.SCL
  N8: 元件1.IO21, Grove1.SDA
  N9: S1.Pin_3, S1.Pin_4, R1.Pin_0
  N10: S2.Pin_3, S2.Pin_4, R2.Pin_0
  N11: S3.Pin_3, S3.Pin_4, R3.Pin_0

custom parts:
  MH-FMD buzzer: MH-FMD buzzer.
  WS2812 RGB LED strip: WS2812 strip
